# Fritzing sketch SchematicV1 (saved by Fritzing 1.0.6)
breadboards: 1

parts:
  U1 = ESP32-38PinWide [part_number=_]
  U2 = Voltage Regulator - 5V [package="TO220 [THT]"]
  C3 = Ceramic Capacitor [capacitance=100nF voltage=35V package="100 mil [THT, multilayer]"]
  C2 = Ceramic Capacitor [capacitance=100nF voltage=35V package="100 mil [THT, multilayer]"]
  Hall_1 = KY-003 Hall Magnetic Sensor Module [package="Breakout board"]
  J1 = Basic Servo
  C4 = Electrolytic Capacitor [package="2cm H-Type"]
  C5 = Electrolytic Capacitor [package="2cm H-Type"]
  BAT1 = Battery Holders [package=lipo-1100mAh]
  C1 = Electrolytic Capacitor [package="2cm H-Type"]

nets:
  N1: U1.GPIO35, Hall_1.S
  GND: U1.GND, U2.GND, C3.0, C2.0, Hall_1.-, J1.gnd, C4.-, C5.-, BAT1.-, C1.-
  VIN: U1.VIN, U2.output_voltage, C3.1, Hall_1.Vin, J1.vcc, C4.+, C5.+
  N2: U1.GPIO18, J1.pulse
  N3: U2.input_voltage, C2.1, BAT1.+, C1.+

custom parts:
  ESP32-38PinWide: Generic 38-Pin ESP32 with wide format (only access to one side of pins on a breadboard) based on Stephen Lilley's HiLetgo ESP-WROOM-32 ESP32 ESP-32S Development Board.
  KY-003 Hall Magnetic Sensor Module: KEYES KY-003 Arduino Hall Magnetic Sensor Module is a switch that will turn on/off in the presence of a magnetic field.
